# Fritzing sketch CelsiusDataToSD (saved by Fritzing 0.9.6b)
breadboards: 1

parts:
  Part1 = Adafruit Feather M0 Adalogger [part_number="Adafruit #2796"]
  Celsius_Fast-Response_±0_1°C_Temperature_Sensor_from_Blue_Robotics = mystery part, 4 pins
  R1 = Resistor [tolerance=±5% power=0.25 resistance=10k package=THT]
  R2 = Resistor [tolerance=±5% power=0.25 resistance=10k package=THT]

nets:
  N1: Part1.GND, Celsius_Fast-Response_±0_1°C_Temperature_Sensor_from_Blue_Robotics.pin3
  N2: Part1.+3V3, R1.Pin_1, R2.Pin_1
  N3: Part1.SCL, Celsius_Fast-Response_±0_1°C_Temperature_Sensor_from_Blue_Robotics.pin1, R2.Pin_0
  N4: Part1.SDA, Celsius_Fast-Response_±0_1°C_Temperature_Sensor_from_Blue_Robotics.pin4, R1.Pin_0

custom parts:
  Adafruit Feather M0 Adalogger: This is the Adafruit Feather M0 Adalogger - our take on an 'all-in-one' Cortex M0 datalogger (or data-reader) with built in USB and battery charging. Its an Adafruit Feather M0 with a microSD holder ready to rock! We have other boards in the Feather family, check'em out here At the Feather M0's heart is an ATSAMD21G18 ARM Cortex M0 processor, clocked at 48 MHz and at 3.3V logic, the same one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
