# Fritzing sketch Feather_LiquidSensor_sketch (saved by Fritzing 0.9.6b)

parts:
  Part1 = Adafruit Feather ESP32-S2 [part_number="Adafruit #5000"]
  U1 = mystery part, 3 pins [chip_label=Sensor]

nets:
  N1: Part1.GND, U1.pin2
  N2: Part1.3.3V, U1.pin3
  N3: Part1.D5, U1.pin1

notes:
  Sensor: Optomax Digital Liquid Level Sensor (product ID: 3397) from Adafruit

custom parts:
  Adafruit Feather ESP32-S2: What's Feather-shaped and has an ESP32-S2 WiFi module? What has a STEMMA QT connector for I2C devices and a built in ambient sensor? What has your favorite Espressif WiFi microcontroller and lots of Flash and RAM memory for your next IoT project? What will make your next IoT project sensor project flyyyyy? That's right - it's the new Adafruit ESP32-S2 Feather and Adafruit ESP32-S2 Feather with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
