# Fritzing sketch FiveLEDs_sketch (saved by Fritzing 0.9.6b)
breadboards: 1

parts:
  Part1 = Arduino Uno (Rev3)
  LED1 = smd LED [color="White (4500K)" package="0603 [SMD]"]
  R1 = Resistor [tolerance=±5% resistance=4.7k package="0402 [SMD]"]
  LED2 = smd LED [color="Red (633nm)" package="0603 [SMD]"]
  R2 = Resistor [tolerance=±5% resistance=220 package="0402 [SMD]"]
  LED3 = smd LED [color="Yellow (585nm)" package="0603 [SMD]"]
  R3 = Resistor [tolerance=±5% resistance=220 package="0402 [SMD]"]
  LED4 = smd LED [color="Green (570nm)" package="0603 [SMD]"]
  R4 = Resistor [tolerance=±5% resistance=220 package="0402 [SMD]"]
  LED5 = smd LED [color="Blue (470nm)" package="0603 [SMD]"]
  R5 = Resistor [tolerance=±5% resistance=4.7k package="0402 [SMD]"]

nets:
  N1: Part1.D9_PWM, LED2.anode
  N2: Part1.D11_PWM/MOSI, LED1.anode
  N3: Part1.D3_PWM, LED5.anode
  N4: Part1.D5_PWM, LED4.anode
  N5: Part1.D6_PWM, LED3.anode
  N6: Part1.GND, R1.Pin_0, R2.Pin_0, R3.Pin_0, R4.Pin_0, R5.Pin_0
  N7: LED1.cathode, R1.Pin_1
  N8: LED2.cathode, R2.Pin_1
  N9: LED3.cathode, R3.Pin_1
  N10: LED4.cathode, R4.Pin_1
  N11: LED5.cathode, R5.Pin_1
