# Fritzing sketch LEDcalibration_sketch (saved by Fritzing 0.9.6b)
breadboards: 1

parts:
  Part1 = Arduino Uno (Rev3)
  LED1 = smd LED [color="Red (635nm)" package="0603 [SMD]"]
  R1 = Resistor [tolerance=±5% resistance=220 package="0402 [SMD]"]
  Note_actual_phototransistor_used_is_the_HW5P-1_model_from_Shenzhen_Haiwang_Sensor_Co = LTR-301 [package=ltr-301]
  R2 = Resistor [tolerance=±5% resistance=10k package="0402 [SMD]"]

nets:
  N1: Part1.A0, Note_actual_phototransistor_used_is_the_HW5P-1_model_from_Shenzhen_Haiwang_Sensor_Co.E, R2.Pin_1
  N2: Part1.D3_PWM, LED1.anode
  N3: Part1.5V, Note_actual_phototransistor_used_is_the_HW5P-1_model_from_Shenzhen_Haiwang_Sensor_Co.C
  N4: Part1.GND, R1.Pin_0, R2.Pin_0
  N5: LED1.cathode, R1.Pin_1
