# Fritzing sketch MeasureDepthBR_ArduinoUNO_sketch (saved by Fritzing 0.9.6b)
breadboards: 1

parts:
  U1 = mystery part, 4 pins [chip_label=Bar100]  # not connected
  Part1 = Arduino Uno (Rev3)
  U3 = mystery part, 8 pins [chip_label=Converter]

nets:
  N1: Part1.A4/SDA, U3.pin3
  N2: Part1.A5/SCL, U3.pin2
  N3: Part1.5V, U3.pin1
  N4: Part1.GND, U3.pin4

notes:
  Bar100 sensor from Blue Robotics is connected to converter via a connector
  Green: SCL
  White: SDA
  Converter: I2C level converter from Blue Robotics
  NOTE: Adafruit datalogging arduino shield with SD card mounted to Uno
