# Fritzing sketch MeasureTempBR_sketch (saved by Fritzing 0.9.6b)
breadboards: 1

parts:
  R2 = Resistor [tolerance=±5% resistance=10k package="0402 [SMD]"]
  Part2 = Adafruit Feather M0 Adalogger [part_number="Adafruit #2796"]
  R3 = Resistor [tolerance=±5% resistance=10k package="0402 [SMD]"]
  U1 = mystery part, 4 pins [chip_label="Temp Sensor"]

nets:
  N1: R2.Pin_0, Part2.+3V3, R3.Pin_0, U1.pin1
  N2: R2.Pin_1, Part2.SCL, U1.pin3
  N3: Part2.GND, U1.pin2
  N4: Part2.SDA, R3.Pin_1, U1.pin4

notes:
  Celsius sensor from Blue Robotics
  Green: SCL
  White: SDA

custom parts:
  Adafruit Feather M0 Adalogger: This is the Adafruit Feather M0 Adalogger - our take on an 'all-in-one' Cortex M0 datalogger (or data-reader) with built in USB and battery charging. Its an Adafruit Feather M0 with a microSD holder ready to rock! We have other boards in the Feather family, check'em out here At the Feather M0's heart is an ATSAMD21G18 ARM Cortex M0 processor, clocked at 48 MHz and at 3.3V logic, the same one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
