# Fritzing sketch Metro_LightSensor_sketch (saved by Fritzing 0.9.6b)

parts:
  Part1 = Adafruit Metro ESP32-S2 [part_number="Adafruit #4775"]
  Part3 = Adafruit TSL2591 High Dynamic Range Digital Light Sensor [part_number="Adafruit #1980"]

nets:
  GND: Part1.GND, Part3.GND
  3.3V: Part1.3.3V, Part3.VCC
  N1: Part1.SDA, Part3.SDA
  N2: Part1.SCL, Part3.SCL

notes:
  STEMMA QT cable

custom parts:
  Adafruit Metro ESP32-S2: What's Metro shaped and has an ESP32-S2 WiFi module? What has a STEMMA QT connector for I2C devices, and a Lipoly charger circuit? What's finishing up testing and nearly ready for fabrication? That's right - its the new Adafruit Metro ESP32-S2! With native USB and a load of PSRAM this board is perfect for use with CircuitPython or Arduino, to add low-cost WiFi while keeping shield-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
  Adafruit TSL2591 High Dynamic Range Digital Light Sensor: When the future is dazzlingly-bright, this ultra-high-range luminosity sensor will help you measure it. The TSL2591 luminosity sensor is an advanced digital light sensor, ideal for use in a wide range of light situations. Compared to low cost CdS cells, this sensor is more precise, allowing for exact lux calculations and can be configured for different gain/timing ranges to detect light ranges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
