# Fritzing sketch StepperMotor_sketch (saved by Fritzing 0.9.6b)

parts:
  Part1 = Arduino Uno (Rev3)
  MOTOR1 = Adafruit Gear-Reduced Stepper Motor (small)
  Part3 = Adafruit DRV8833 DC/Stepper Motor Driver [part_number="Adafruit #3297"]

nets:
  GND: Part1.GND, MOTOR1.RED, Part3.GND
  N1: Part1.D4, Part3.AIN1
  N2: Part1.D5_PWM, Part3.AIN2
  N3: Part1.D6_PWM, Part3.BIN2
  N4: Part1.D7, Part3.BIN1
  N5: Part1.5V, Part3.!SLEEP
  N6: Part1.VIN, Part3.VMOTOR
  N7: MOTOR1.ORANGE, Part3.BOUT2
  N8: MOTOR1.YELLOW, Part3.AOUT1
  N9: MOTOR1.PINK, Part3.BOUT1
  N10: MOTOR1.BLUE, Part3.AOUT2

custom parts:
  Adafruit Gear-Reduced Stepper Motor (small): Adafruit gear-reduction stepper motor (small)
  Adafruit DRV8833 DC/Stepper Motor Driver: Spin two DC motors or step one bi-polar or uni-polar stepper with up to 1.2A per channel using the DRV8833. This motor driver chip is a nice alternative to the TB6612 driver. Like that chip, you get 2 full H-bridges, but this chip is better for low voltage uses (can run from 2.7V up to 10.8V motor power) and has built in current limiting capability. We set it up for 1A current limiting so you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
