# Fritzing sketch Temperature_sketch (saved by Fritzing 0.9.6b)
breadboards: 1

parts:
  Part1 = Arduino Uno (Rev3)
  R2 = Resistor [tolerance=±5% resistance=4.7k package="0402 [SMD]"]
  DS1 = DS18B20 1-Wire Temperature Sensor [part_number=DS18B20]  # not connected

nets:
  N1: Part1.D4, R2.Pin_1
  N2: Part1.5V, R2.Pin_0
