# Fritzing sketch TenLEDs_sketch (saved by Fritzing 0.9.6b)
breadboards: 1

parts:
  Part1 = Arduino Uno (Rev3)
  R1 = Resistor [tolerance=±5% resistance=4.7k package="0402 [SMD]"]
  R2 = Resistor [tolerance=±5% resistance=220 package="0402 [SMD]"]
  R3 = Resistor [tolerance=±5% resistance=220 package="0402 [SMD]"]
  R4 = Resistor [tolerance=±5% resistance=220 package="0402 [SMD]"]
  R5 = Resistor [tolerance=±5% resistance=4.7k package="0402 [SMD]"]
  LED6 = smd LED [color="Blue (470nm)" package="0603 [SMD]"]
  LED7 = smd LED [color="Green (570nm)" package="0603 [SMD]"]
  LED8 = smd LED [color="Yellow (585nm)" package="0603 [SMD]"]
  LED9 = smd LED [color="Red (633nm)" package="0603 [SMD]"]
  R6 = Resistor [tolerance=±5% resistance=4.7k package="0402 [SMD]"]
  R7 = Resistor [tolerance=±5% resistance=220 package="0402 [SMD]"]
  R8 = Resistor [tolerance=±5% resistance=220 package="0402 [SMD]"]
  R9 = Resistor [tolerance=±5% resistance=220 package="0402 [SMD]"]
  R10 = Resistor [tolerance=±5% resistance=4.7k package="0402 [SMD]"]
  LED13 = smd LED [color="White (4500K)" package="0603 [SMD]"]
  LED14 = smd LED [color="Red (633nm)" package="0603 [SMD]"]
  LED15 = smd LED [color="Yellow (585nm)" package="0603 [SMD]"]
  LED16 = smd LED [color="Green (570nm)" package="0603 [SMD]"]
  LED17 = smd LED [color="Blue (470nm)" package="0603 [SMD]"]
  LED18 = smd LED [color="White (4500K)" package="0603 [SMD]"]

nets:
  N1: Part1.D9_PWM, LED14.anode
  N2: Part1.D10_PWM/SS, LED18.anode
  N3: Part1.D11_PWM/MOSI, LED13.anode
  N4: Part1.D2, LED6.anode
  N5: Part1.D3_PWM, LED17.anode
  N6: Part1.D4, LED7.anode
  N7: Part1.D5_PWM, LED16.anode
  N8: Part1.D6_PWM, LED8.anode
  N9: Part1.D7, LED15.anode
  N10: Part1.GND, R1.Pin_0, R2.Pin_0, R3.Pin_0, R4.Pin_0, R5.Pin_0, R6.Pin_1, R7.Pin_1, R8.Pin_1, R9.Pin_1, R10.Pin_1
  N11: R1.Pin_1, LED13.cathode
  N12: R2.Pin_1, LED14.cathode
  N13: R3.Pin_1, LED15.cathode
  N14: R4.Pin_1, LED16.cathode
  N15: R5.Pin_1, LED17.cathode
  N16: LED6.cathode, R6.Pin_0
  N17: LED7.cathode, R7.Pin_0
  N18: LED8.cathode, R8.Pin_0
  N19: LED9.cathode, R9.Pin_0
  N20: R10.Pin_0, LED18.cathode
