# Fritzing sketch Thermistor (saved by Fritzing 0.9.6b)
breadboards: 1

parts:
  Part1 = Arduino Uno (Rev3)
  R2 = Resistor [tolerance=±5% power=0.25 resistance=10k package=THT]
  R3 = Temperature Sensor (Thermistor) [thermistor_type=NTC package=THT]

nets:
  N1: Part1.A0, R2.Pin_1, R3.pin_1
  N2: Part1.AREF, Part1.3V3, R2.Pin_0
  N3: Part1.GND, R3.pin_0
