# Fritzing sketch Vibration_sketch (saved by Fritzing 0.9.6b)
breadboards: 1

parts:
  Part1 = Arduino Uno (Rev3)
  LED2 = smd LED [color="Red (633nm)" package="0603 [SMD]"]
  R2 = Resistor [tolerance=±5% resistance=220 package="0402 [SMD]"]
  U1 = Vibration Motor- ROB-08449 [package=vibe-motor-10mm]

nets:
  N1: Part1.D9_PWM, LED2.anode
  N2: Part1.D10_PWM/SS, U1.-
  N3: Part1.GND, R2.Pin_0, U1.+
  N4: LED2.cathode, R2.Pin_1
