# Fritzing sketch Vibration_with_button_sketch (saved by Fritzing 0.9.6b)
breadboards: 1

parts:
  Part1 = Arduino Uno (Rev3)
  LED2 = smd LED [color="Red (633nm)" package="0603 [SMD]"]
  R2 = Resistor [tolerance=±5% resistance=220 package="0402 [SMD]"]
  U1 = Vibration Motor- ROB-08449 [package=vibe-motor-10mm]
  S1 = Momentary Switch [package=ksa_sealed_tac_switch]
  R3 = Resistor [tolerance=±5% resistance=1M package="0402 [SMD]"]

nets:
  N1: Part1.D9_PWM, LED2.anode
  N2: Part1.D10_PWM/SS, U1.-
  N3: Part1.D2, S1.3, R3.Pin_1
  N4: Part1.5V, S1.1
  N5: Part1.GND, R2.Pin_0, U1.+, R3.Pin_0
  N6: LED2.cathode, R2.Pin_1
